// Logisim project Complete Circuit.circ as structural Verilog: 4 circuits, main circuit main
module main (
  output [19:0] out_1,
  output [2:0] RS,
  output [19:0] out_3,
  output [2:0] RT,
  output [19:0] out_5,
  output [2:0] RD,
  output [3:0] OP_code
);

  wire alu_1_zero, and_1_out, Clock_out, control_unit_1_binv, control_unit_1_branch, control_unit_1_cin,
       control_unit_1_jump, control_unit_1_memread, control_unit_1_memtoreg, control_unit_1_memwrite,
       control_unit_1_ramen, control_unit_1_regdest, control_unit_1_rt_im, control_unit_1_writeen,
       PC_clear_out, Ramclr_out, Regclr_out;
  wire [1:0] control_unit_1_aluop;
  wire [2:0] multiplexer_1_out;
  wire [15:0] adder_1_out, bit_extender_1_out, bit_extender_3_out, bit_extender_4_out, multiplexer_3_out,
       multiplexer_4_out, PC_q;
  wire [19:0] bit_extender_2_out, multiplexer_5_out, ram_1_data, register_1_read_data_2;
  wire [19:3] rom_1_data;

  Button Clock (.out(Clock_out));
  Register_part #(.width(16)) PC (.D(multiplexer_4_out), .Q(PC_q), .clk(Clock_out), .clr(PC_clear_out));  // open: en
  Button Regclr (.out(Regclr_out));
  Button Ramclr (.out(Ramclr_out));
  Button PC_clear (.out(PC_clear_out));
  Adder #(.width(16)) adder_1 (.a(16'h1), .b(PC_q), .out(adder_1_out));  // open: cin, cout
  ROM #(.addrWidth(16), .dataWidth(20)) rom_1 (
    .addr(PC_q), .data({rom_1_data[19:16], OP_code, rom_1_data[11], RS, rom_1_data[7], RT, rom_1_data[3], RD}));  // open: sel
  assign bit_extender_1_out = {{7{1'b0}}, {RS[0], rom_1_data[7], RT, rom_1_data[3], RD}};  // Bit_Extender bit_extender_1
  Multiplexer #(.width(3), .enable("false")) multiplexer_1 (
    .in0(RD), .in1(RT), .out(multiplexer_1_out), .sel(control_unit_1_regdest));
  Control_UNit control_unit_1 (
    .in_1(OP_code), .AluOp(control_unit_1_aluop), .Cin(control_unit_1_cin), .Binv(control_unit_1_binv),
    .WriteEn(control_unit_1_writeen), .RamEn(control_unit_1_ramen), .MemWrite(control_unit_1_memwrite),
    .MemRead(control_unit_1_memread), .MemToReg(control_unit_1_memtoreg), .RegDest(control_unit_1_regdest),
    .RT_IM(control_unit_1_rt_im), .Branch(control_unit_1_branch), .Jump(control_unit_1_jump));
  Register register_1 (
    .Clear(Regclr_out), .Write_Data(multiplexer_5_out), .Read_register_1_RS(RS),
    .Write_register(multiplexer_1_out), .Read_register_2_RT(RT), .Read_data_1(out_3),
    .Read_data_2(register_1_read_data_2), .Write_Control(control_unit_1_writeen), .Clock(Clock_out));
  assign bit_extender_2_out = {{17{1'b0}}, RD};  // Bit_Extender bit_extender_2
  Multiplexer #(.width(20), .enable("false")) multiplexer_2 (
    .in0(register_1_read_data_2), .in1(bit_extender_2_out), .out(out_5), .sel(control_unit_1_rt_im));
  Bit_Extender #(.in_width(20)) bit_extender_3 (.in(bit_extender_2_out), .out(bit_extender_3_out));
  ALU alu_1 (
    .ALUOP(control_unit_1_aluop), .Cin(control_unit_1_cin), .Binv(control_unit_1_binv), .F(out_1),
    .Zero(alu_1_zero), .A(out_3), .B(out_5));  // open: Cout
  and and_1 (and_1_out, alu_1_zero, control_unit_1_branch);
  Bit_Extender #(.in_width(20)) bit_extender_4 (.in(out_1), .out(bit_extender_4_out));
  Multiplexer #(.width(16), .enable("false")) multiplexer_3 (
    .in0(adder_1_out), .in1(bit_extender_3_out), .out(multiplexer_3_out), .sel(and_1_out));
  Multiplexer #(.width(16), .enable("false")) multiplexer_4 (
    .in0(multiplexer_3_out), .in1(bit_extender_1_out), .out(multiplexer_4_out), .sel(control_unit_1_jump));
  RAM #(.addrWidth(16), .dataWidth(20), .bus("separate")) ram_1 (
    .addr(bit_extender_4_out), .din(register_1_read_data_2), .data(ram_1_data),
    .str(control_unit_1_memwrite), .sel(control_unit_1_ramen), .clk(Clock_out), .ld(control_unit_1_memread),
    .clr(Ramclr_out));
  Multiplexer #(.width(20), .enable("false")) multiplexer_5 (
    .in0(out_1), .in1(ram_1_data), .out(multiplexer_5_out), .sel(control_unit_1_memtoreg));

  // Notes on the sheet:
  //   Adder
  //   Ins Memory
endmodule

module ALU (
  input  [19:0] A,
  input  [19:0] B,
  input  [1:0] ALUOP,
  input  Cin,
  input  Binv,
  output [19:0] F,
  output Zero,
  output Cout
);

  wire comparator_1_lt;
  wire [4:0] bit_extender_1_out;
  wire [19:0] adder_1_out, and_1_out, bit_extender_2_out, multiplexer_1_out, not_1_out, shifter_1_out;

  Bit_Extender #(.in_width(20), .out_width(5)) bit_extender_1 (.in(B), .out(bit_extender_1_out));
  assign and_1_out = A & B;  // AND_Gate and_1, 20 bits wide
  Comparator #(.width(20)) comparator_1 (.a(A), .b(B), .eq(Zero), .lt(comparator_1_lt));  // open: gt
  Multiplexer #(.width(20), .enable("false")) multiplexer_1 (
    .in0(B), .in1(not_1_out), .out(multiplexer_1_out), .sel(Binv));
  assign not_1_out = ~B;  // NOT_Gate not_1, 20 bits wide
  Shifter #(.width(20)) shifter_1 (.in(A), .\dist (bit_extender_1_out), .out(shifter_1_out));
  assign bit_extender_2_out = {{19{1'b0}}, comparator_1_lt};  // Bit_Extender bit_extender_2
  Adder #(.width(20)) adder_1 (.a(A), .b(multiplexer_1_out), .out(adder_1_out), .cin(Cin), .cout(Cout));
  Multiplexer #(.select(2), .width(20), .enable("false")) multiplexer_2 (
    .in0(shifter_1_out), .in1(and_1_out), .in2(bit_extender_2_out), .in3(adder_1_out), .out(F), .sel(ALUOP));
endmodule

module Control_UNit (
  input  [3:0] in_1,
  output [1:0] AluOp,
  output Cin,
  output Binv,
  output WriteEn,
  output RamEn,
  output MemWrite,
  output MemRead,
  output MemToReg,
  output RegDest,
  output RT_IM,
  output Branch,
  output Jump
);

  wire decoder_1_out0, decoder_1_out2, decoder_1_out5, decoder_1_out6, decoder_1_out9, decoder_1_out10;

  Decoder #(.select(4), .enable("false")) decoder_1 (
    .out0(decoder_1_out0), .out1(MemRead), .out2(decoder_1_out2), .out3(MemWrite), .out4(Branch),
    .out5(decoder_1_out5), .out6(decoder_1_out6), .out7(Binv), .out8(Jump), .out9(decoder_1_out9),
    .out10(decoder_1_out10), .sel(in_1));  // open: out11, out12, out13, out14, out15
  or or_1 (AluOp[0], MemRead, decoder_1_out2, MemWrite, decoder_1_out6, Binv, decoder_1_out10);
  or or_2 (AluOp[1], MemRead, decoder_1_out2, MemWrite, decoder_1_out5, Binv, decoder_1_out10);
  or or_3 (WriteEn, MemRead, decoder_1_out2, decoder_1_out5, decoder_1_out6, Binv, decoder_1_out9, decoder_1_out10);
  or or_4 (RamEn, MemRead, MemWrite);
  or or_5 (RegDest, MemRead, decoder_1_out2);
  or or_6 (RT_IM, MemRead, decoder_1_out2, MemWrite);

  assign Cin = Binv;
  assign MemToReg = MemRead;
endmodule

module Register (
  input  Clear,
  input  [19:0] Write_Data,
  input  Clock,
  input  [2:0] Read_register_1_RS,
  input  [2:0] Write_register,
  input  Write_Control,
  input  [2:0] Read_register_2_RT,
  output [19:0] Read_data_1,
  output [19:0] Read_data_2
);

  wire and_1_out, and_2_out, and_3_out, and_4_out, and_5_out, and_6_out, and_7_out, and_8_out,
       decoder_1_out0, decoder_1_out1, decoder_1_out2, decoder_1_out3, decoder_1_out4, decoder_1_out5,
       decoder_1_out6, decoder_1_out7;
  wire [19:0] r0_q, r1_q, r2_q, r3_q, r4_q, r5_q, r6_q, r7_q;

  Decoder #(.select(3), .enable("false")) decoder_1 (
    .out0(decoder_1_out0), .out1(decoder_1_out1), .out2(decoder_1_out2), .out3(decoder_1_out3),
    .out4(decoder_1_out4), .out5(decoder_1_out5), .out6(decoder_1_out6), .out7(decoder_1_out7),
    .sel(Write_register));
  and and_1 (and_1_out, decoder_1_out0, Write_Control);
  and and_2 (and_2_out, decoder_1_out1, Write_Control);
  and and_3 (and_3_out, decoder_1_out2, Write_Control);
  and and_4 (and_4_out, decoder_1_out3, Write_Control);
  and and_5 (and_5_out, decoder_1_out4, Write_Control);
  and and_6 (and_6_out, decoder_1_out5, Write_Control);
  and and_7 (and_7_out, decoder_1_out6, Write_Control);
  and and_8 (and_8_out, decoder_1_out7, Write_Control);
  Register_part #(.width(20)) r0 (.D(Write_Data), .en(and_1_out), .Q(r0_q), .clk(Clock), .clr(Clear));
  Register_part #(.width(20)) r1 (.D(Write_Data), .en(and_2_out), .Q(r1_q), .clk(Clock), .clr(Clear));
  Register_part #(.width(20)) r2 (.D(Write_Data), .en(and_3_out), .Q(r2_q), .clk(Clock), .clr(Clear));
  Register_part #(.width(20)) r3 (.D(Write_Data), .en(and_4_out), .Q(r3_q), .clk(Clock), .clr(Clear));
  Register_part #(.width(20)) r4 (.D(Write_Data), .en(and_5_out), .Q(r4_q), .clk(Clock), .clr(Clear));
  Register_part #(.width(20)) r5 (.D(Write_Data), .en(and_6_out), .Q(r5_q), .clk(Clock), .clr(Clear));
  Register_part #(.width(20)) r6 (.D(Write_Data), .en(and_7_out), .Q(r6_q), .clk(Clock), .clr(Clear));
  Register_part #(.width(20)) r7 (.D(Write_Data), .en(and_8_out), .Q(r7_q), .clk(Clock), .clr(Clear));
  Multiplexer #(.select(3), .width(20), .enable("false")) multiplexer_1 (
    .in0(r0_q), .in1(r1_q), .in2(r2_q), .in3(r3_q), .in4(r4_q), .in5(r5_q), .in6(r6_q), .in7(r7_q),
    .out(Read_data_1), .sel(Read_register_1_RS));
  Multiplexer #(.select(3), .width(20), .enable("false")) multiplexer_2 (
    .in0(r0_q), .in1(r1_q), .in2(r2_q), .in3(r3_q), .in4(r4_q), .in5(r5_q), .in6(r6_q), .in7(r7_q),
    .out(Read_data_2), .sel(Read_register_2_RT));

  // Notes on the sheet:
  //   8 bit register
endmodule
